// Digital circuit I-mem.dig as structural Verilog
module I_mem (
  input  [15:0] o1,
  input  en,
  input  [15:0] inst,
  output [15:0] _1a
);

  Multiplexer #(.Bits(16)) multiplexer_1 (.sel(en), .in_0(o1), .in_1({{8{1'b0}}, inst[7:0]}), .out(_1a));
endmodule

/* Test case:
en	o1	inst	1a
let ldiop = 0b0010;

loop(i, 100)
    let o = random(1<<16);
    let ra = random(1<<4);
    let imm = random(1<<8);
    (0) (o) (ldiop<<12 | ra<<8 | imm) (o)
    (1) (o) (ldiop<<12 | ra<<8 | imm) (0<<8 | imm)
end loop
*/
