// Digital circuit cpu.dig as structural Verilog
module cpu (
  input  CLK
);

  wire EXEC, FLEN, LDI, LDR, SETH, STR, WE;
  wire [1:0] ALUOP, control_unit_1_dmux;
  wire [2:0] RS1, RS2, WS;
  wire [3:0] alu_1_flag;
  wire [7:0] RAM_d2;
  wire [15:0] alu_1_result, FLIN, ldi_1__1a, multiplexer_1_out, notconnected_1_out, RAM_d1, reg_file_1_out1,
       reg_file_1_out2, reg_file_1_pc;
  wire [15:8] RAM_d2_2;

  control_unit control_unit_1 (
    .INST({RAM_d2_2, RAM_d2}), .Z(FLIN[0]), .DMUX(control_unit_1_dmux), .ALUOP(ALUOP), .RS1(RS1), .RS2(RS2),
    .WS(WS), .WE(WE), .EXEC(EXEC), .SETH(SETH), .FLEN(FLEN), .STR(STR), .LDR(LDR), .LDI(LDI));
  Multiplexer #(.Selector_Bits(2), .Bits(16)) multiplexer_1 (
    .sel(control_unit_1_dmux), .in_0(alu_1_result), .in_1(RAM_d1), .in_2({{8{1'b0}}, RAM_d2}),
    .in_3(notconnected_1_out), .out(multiplexer_1_out));
  // NotConnected on notconnected_1_out
  reg_file reg_file_1 (
    .IN(multiplexer_1_out), .clk(CLK), .RS1(RS1), .RS2(RS2), .WS(WS), .WE(WE), .EXEC(EXEC), .SETH(SETH),
    .FLIN(FLIN), .OUT1(reg_file_1_out1), .OUT2(reg_file_1_out2), .PC(reg_file_1_pc));
  ldi ldi_1 (.o1(reg_file_1_out1), .en(LDI), .inst({RAM_d2_2, RAM_d2}), ._1a(ldi_1__1a));
  alu alu_1 (.A(reg_file_1_out1), .B(reg_file_1_out2), .RESULT(alu_1_result), .ALUOP(ALUOP), .FLAG(alu_1_flag));
  RAMDualAccess #(.AddrBits(16), .isProgramMemory("true"), .Bits(16)) RAM (
    .str(STR), .C(CLK), .ld(LDR), .A1(ldi_1__1a), .Din1(reg_file_1_out2), .A2(reg_file_1_pc), .D1(RAM_d1),
    .D2({RAM_d2_2, RAM_d2}));
  Register #(.Bits(16)) fl (.D({{12{1'b0}}, alu_1_flag}), .C(CLK), .en(FLEN), .Q(FLIN));
endmodule
